# Fritzing sketch XIAO SOCD Cleaner (saved by Fritzing 0.9.5d)
breadboards: 1

parts:
  part = seeeduino-xiao
  R1 = Resistor [tolerance=±5% resistance=100 package=THT]
  PC847 = IC, DIP package, 16 pins [chip_label=PC847]
  R2 = Resistor [tolerance=±5% resistance=100 package=THT]
  R3 = Resistor [tolerance=±5% resistance=100 package=THT]
  R4 = Resistor [tolerance=±5% resistance=100 package=THT]
  Output = female alternating pin header, 5 pins [form="♀ (female)"]
  Input = female alternating pin header, 5 pins [form="♀ (female)"]
  POWER = female pin header, 2 pins [form="♀ (female)"]

nets:
  N1: part.D1, Input.pin4
  N2: part.D2, Input.pin3
  N3: part.D3, Input.pin2
  N4: part.D4, Input.pin1
  N5: part.D5, R1.Pin_1
  N6: part.D8, R4.Pin_1
  N7: part.D9, R3.Pin_1
  N8: part.D10, R2.Pin_1
  N9: part.3V3, POWER.pin2
  N10: part.GND, PC847.pin2, PC847.pin4, PC847.pin6, PC847.pin8, Input.pin5, POWER.pin1
  N11: R1.Pin_0, PC847.pin1
  N12: PC847.pin3, R2.Pin_0
  N13: PC847.pin5, R3.Pin_0
  N14: PC847.pin7, R4.Pin_0
  N15: PC847.pin9, PC847.pin11, PC847.pin13, PC847.pin15, Output.pin5
  N16: PC847.pin10, Output.pin4
  N17: PC847.pin12, Output.pin3
  N18: PC847.pin14, Output.pin2
  N19: PC847.pin16, Output.pin1

custom parts:
  seeeduino-xiao: Seeeduino XIAO processor board.
